// Logisim project 2_nand_and.circ as structural Verilog: 1 circuit, main circuit main
module main (
  input  a,
  input  b,
  output out
);

  wire N1_out;

  nand N1 (N1_out, a, b);
  nand N2 (out, N1_out, N1_out);

  // Notes on the sheet:
  //   IN:
  //   Nand
  //   aNandb
  //   Nand
  //   OUT:
endmodule
