// Logisim project memory_cell.circ as structural Verilog: 1 circuit, main circuit main
module main (
  input  i,
  input  s,
  output o
);

  wire N1_out, N2_out, N3_out;

  nand N1 (N1_out, i, s);
  nand N2 (N2_out, N1_out, s);
  nand N4 (o, N1_out, N3_out);
  nand N3 (N3_out, o, N2_out);

  // Notes on the sheet:
  //   fromi
  //   ctrl
  //   fdbck
endmodule
